# Fritzing sketch web-relay-board-nodemcu-pcb-36 (saved by Fritzing 0.9.2b)
circuit board: 5cm x 5cm
breadboards: 1

parts:
  1 = SHIFT REGISTER [package=dil16]
  2 = SHIFT REGISTER [package=dil16]
  1_2 = Darlington Driver [package=dil18]
  2_2 = Darlington Driver [package=dil18]
  5v = Pad [width=3.25 height=2 connect=center]
  2_3 = Pad [width=3.25 height=2 connect=center]
  4 = Pad [width=3.25 height=2 connect=center]
  6 = Pad [width=3.25 height=2 connect=center]
  8 = Pad [width=3.25 height=2 connect=center]
  10 = Pad [width=3.25 height=2 connect=center]
  12 = Pad [width=3.25 height=2 connect=center]
  14 = Pad [width=3.25 height=2 connect=center]
  16 = Pad [width=3.25 height=2 connect=center]
  GND = Pad [width=3.25 height=2 connect=center]
  5v_2 = Pad [width=3.25 height=2 connect=center]
  1_3 = Pad [width=3.25 height=2 connect=center]
  3 = Pad [width=3.25 height=2 connect=center]
  5 = Pad [width=3.25 height=2 connect=center]
  9 = Pad [width=3.25 height=2 connect=center]
  7 = Pad [width=3.25 height=2 connect=center]
  13 = Pad [width=3.25 height=2 connect=center]
  11 = Pad [width=3.25 height=2 connect=center]
  15 = Pad [width=3.25 height=2 connect=center]
  GND_2 = Pad [width=3.25 height=2 connect=center]
  WeMos_D1_Mini1 = WeMos D1 Mini
  part = Screw terminal - 2 pins [package=THT]
  SFH = IC, DIP package, 4 pins [chip_label=IC]
  1k2 = Resistor [tolerance=±5% resistance=1k package=THT]
  3k3 = Resistor [tolerance=±5% resistance=3.3k package=THT]
  HTU21D = female pin header, 4 pins [form="♀ (female)"]

nets:
  N1: 1.QB, 1_2.2
  N2: 1.QC, 1_2.3
  N3: 1.QD, 1_2.4
  N4: 1.QE, 1_2.5
  N5: 1.QF, 1_2.6
  N6: 1.QG, 1_2.7
  N7: 1.QH, 1_2.8
  GND: 1.GND, 1.G, 2.GND, 2.G, 1_2.9, 2_2.9, GND.pad, GND_2.pad, WeMos_D1_Mini1.G, SFH.pin3, HTU21D.pin2
  N8: 1.QH*, 2.SER
  VCC: 1.SCL, 1.VCC, 2.SCL, 2.VCC
  N9: 1.SCK, 2.SCK, WeMos_D1_Mini1.D6
  N10: 1.RCK, 2.RCK, WeMos_D1_Mini1.D8
  N11: 1.SER, WeMos_D1_Mini1.D7
  N12: 1.QA, 1_2.1
  N13: 2.QB, 2_2.2
  N14: 2.QC, 2_2.3
  N15: 2.QD, 2_2.4
  N16: 2.QE, 2_2.5
  N17: 2.QF, 2_2.6
  N18: 2.QG, 2_2.7
  N19: 2.QH, 2_2.8
  N20: 2.QA, 2_2.1
  N21: 1_2.10, 2_2.10, 5v.pad, 5v_2.pad, WeMos_D1_Mini1.5V
  N22: 1_2.11, 8.pad
  N23: 1_2.12, 7.pad
  N24: 1_2.13, 6.pad
  N25: 1_2.14, 5.pad
  N26: 1_2.15, 4.pad
  N27: 1_2.16, 3.pad
  N28: 1_2.17, 2_3.pad
  N29: 1_2.18, 1_3.pad
  N30: 2_2.11, 16.pad
  N31: 2_2.12, 15.pad
  N32: 2_2.13, 14.pad
  N33: 2_2.14, 13.pad
  N34: 2_2.15, 12.pad
  N35: 2_2.16, 11.pad
  N36: 2_2.17, 10.pad
  N37: 2_2.18, 9.pad
  N38: WeMos_D1_Mini1.3V3, 3k3.Pin_0, HTU21D.pin1
  N39: WeMos_D1_Mini1.D1, HTU21D.pin4
  N40: WeMos_D1_Mini1.D2, HTU21D.pin3
  N41: WeMos_D1_Mini1.D5, SFH.pin4, 3k3.Pin_1
  N42: part.pin1, 1k2.Pin_0
  N43: part.pin2, SFH.pin2
  N44: SFH.pin1, 1k2.Pin_1

notes:
  SainSmart 16 relays 5v
  Node MCU (3.3v)
  5v
  3.3v

custom parts:
  WeMos D1 Mini: The D1 mini is a mini wifi board based on ESP-8266EX.
