# Fritzing sketch web-relay-board-nodemcu-pcb (saved by Fritzing 0.9.2b)
circuit board: 5cm x 5cm
breadboards: 1

parts:
  J1 = female pin header, 15 pins [form="♀ (female)"]
  J2 = female pin header, 15 pins [form="♀ (female)"]
  J3 = female pin header, 18 pins [form="♀ (female)"]
  1 = SHIFT REGISTER [package=dil16]
  2 = SHIFT REGISTER [package=dil16]
  1_2 = Darlington Driver [package=dil18]
  2_2 = Darlington Driver [package=dil18]

nets:
  N1: J1.pin1, J3.pin18, 1_2.10, 2_2.10
  GND: J1.pin2, J2.pin14, J3.pin1, 1.GND, 1.G, 2.GND, 2.G, 1_2.9, 2_2.9
  VCC: J1.pin5, 1.SCL, 1.VCC, 2.SCL, 2.VCC
  N2: J2.pin8, 1.SCK, 2.SCK
  N3: J2.pin10, 1.SER
  N4: J2.pin11, 1.RCK, 2.RCK
  N5: J3.pin2, 1_2.18
  N6: J3.pin3, 1_2.17
  N7: J3.pin4, 1_2.16
  N8: J3.pin5, 1_2.15
  N9: J3.pin6, 1_2.14
  N10: J3.pin7, 1_2.13
  N11: J3.pin8, 1_2.12
  N12: J3.pin9, 1_2.11
  N13: J3.pin10, 2_2.18
  N14: J3.pin11, 2_2.17
  N15: J3.pin12, 2_2.16
  N16: J3.pin13, 2_2.15
  N17: J3.pin14, 2_2.14
  N18: J3.pin15, 2_2.13
  N19: J3.pin16, 2_2.12
  N20: J3.pin17, 2_2.11
  N21: 1.QB, 1_2.2
  N22: 1.QC, 1_2.3
  N23: 1.QD, 1_2.4
  N24: 1.QE, 1_2.5
  N25: 1.QF, 1_2.6
  N26: 1.QG, 1_2.7
  N27: 1.QH, 1_2.8
  N28: 1.QH*, 2.SER
  N29: 1.QA, 1_2.1
  N30: 2.QB, 2_2.2
  N31: 2.QC, 2_2.3
  N32: 2.QD, 2_2.4
  N33: 2.QE, 2_2.5
  N34: 2.QF, 2_2.6
  N35: 2.QG, 2_2.7
  N36: 2.QH, 2_2.8
  N37: 2.QA, 2_2.1

notes:
  SainSmart 16 relays 5v
  Node MCU (3.3v)
  5v
  3.3v
