# Fritzing sketch web-relay-board-nodemcu (saved by Fritzing 0.9.2b)
breadboards: 1

parts:
  U1 = 74HC595 [package="DIP16 [THT]"]
  U2 = 74HC595 [package="DIP16 [THT]"]
  U3 = NodeMCU V1.0
  ULN1 = Darlington Driver [package=dil18]
  ULN2 = Darlington Driver [package=dil18]
  U4 = Header 10 [package=1x10-2mm-smd]
  U5 = Header 10 [package=1x10-2mm-smd]

nets:
  N1: U1.Q1, ULN1.2
  N2: U1.Q2, ULN1.3
  N3: U1.Q3, ULN1.4
  N4: U1.Q4, ULN1.5
  N5: U1.Q5, ULN1.6
  N6: U1.Q6, ULN1.7
  N7: U1.Q7, ULN1.8
  GND: U1.GND, U1.OE, U2.GND, U2.OE, U3.GND, ULN1.9, ULN2.9, U4.1, U5.1
  N8: U1.Q7', U2.DS
  VCC: U1.MR, U1.VCC, U2.MR, U2.VCC, U3.3V3
  N9: U1.SH_CP, U2.SH_CP, U3.D5
  N10: U1.ST_CP, U2.ST_CP, U3.D8
  N11: U1.DS, U3.D7
  N12: U1.Q0, ULN1.1
  N13: U2.Q1, ULN2.2
  N14: U2.Q2, ULN2.3
  N15: U2.Q3, ULN2.4
  N16: U2.Q4, ULN2.5
  N17: U2.Q5, ULN2.6
  N18: U2.Q6, ULN2.7
  N19: U2.Q7, ULN2.8
  N20: U2.Q0, ULN2.1
  N21: U3.Vin, ULN1.10, ULN2.10, U4.10, U5.10
  N22: ULN1.11, U4.9
  N23: ULN1.12, U4.8
  N24: ULN1.13, U4.7
  N25: ULN1.14, U4.6
  N26: ULN1.15, U4.5
  N27: ULN1.16, U4.4
  N28: ULN1.17, U4.3
  N29: ULN1.18, U4.2
  N30: ULN2.11, U5.9
  N31: ULN2.12, U5.8
  N32: ULN2.13, U5.7
  N33: ULN2.14, U5.6
  N34: ULN2.15, U5.5
  N35: ULN2.16, U5.4
  N36: ULN2.17, U5.3
  N37: ULN2.18, U5.2

notes:
  SainSmart 16 relays 5v
  Node MCU (3.3v)
  5v
  3.3v

custom parts:
  NodeMCU V1.0: ESP9266 based NodeMCU
